# Fritzing sketch schematic (saved by Fritzing 0.9.3b)
perfboards: 1

parts:
  TWELITE1 = TWE-Lite DIP [package=DIP]
  Power_plug1_3_3V = Power plug  # not connected
  J1 = female pin header, 4 pins [form="♀ (female)"]
  LED1 = smd LED [color="Green (570nm)" package="0805 [SMD]"]  # not connected
  LED2 = smd LED [color="Green (570nm)" package="0805 [SMD]"]  # not connected
  R1 = Resistor [tolerance=±5% resistance=1k package="0603 [SMD]"]
  U1 = ESP-WROOM-02-AE [part_number=ESP-WROOM-02-AE]
  R2 = Resistor [tolerance=±5% resistance=1k package="0603 [SMD]"]
  J2 = female pin header, 4 pins [form="♀ (female)"]
  J3 = female pin header, 2 pins [form="♀ (female)"]
  J4 = female pin header, 2 pins [form="♀ (female)"]
  J5 = male pin header, 2 pins [form="♂ (male)"]

nets:
  GND: TWELITE1.GND, TWELITE1.M1, J1.pin1, U1.IO15, U1.GND, J2.pin1, J3.pin2, J4.pin2, J5.pin2
  N1: TWELITE1.SCL, U1.RXD, J2.pin2
  N2: TWELITE1.RX, J1.pin2
  N3: TWELITE1.TX, J1.pin3
  VCC: TWELITE1.VCC, J1.pin4, R1.Pin_1, U1.3V3, U1.EN, U1.IO0, J2.pin4, J5.pin1
  N4: R1.Pin_0, J3.pin1
  N5: U1.TXD, J2.pin3
  N6: U1.IO4, R2.Pin_1
  N7: R2.Pin_0, J4.pin1

custom parts:
  TWE-Lite DIP: TOCOS TWE-Lite DIP
  ESP-WROOM-02-AE: ESP-WROOM-02 with the DIP breakout board by Akizuki-Electronics in Japan. See http://akizukidenshi.com/catalog/g/gK-09758/ for the detauls.
